# Fritzing sketch conexiones (saved by Fritzing 1.0.4)
circuit board: 8.46667cm x 5.64444cm
breadboards: 1

parts:
  Componente1 = Arduino Uno (Rev3)
  Componente2 = Arduino Uno (Rev3)
  Componente3 = Arduino Uno (Rev3)
  R1 = Rotary Potentiometer (Small) [maximum_resistance=10kΩ knob_status=50% power=0.5W package=THT]
  LED1 = LED - 5mm [color="Red (633nm)" current=0.030A package="5 mm [THT]"]
  S1 = Pushbutton [package="[THT]"]
  S2 = Pushbutton [package="[THT]"]
  R2 = Resistor [tolerance=±5% power=0.25W resistance=1.5k package=THT]
  R3 = Resistor [tolerance=±5% power=0.25W resistance=1.5k package=THT]

nets:
  N1: Componente1.A0, R1.wiper
  N2: Componente1.A4/SDA, Componente2.A4/SDA, Componente3.A4/SDA
  N3: Componente1.A5/SCL, Componente2.A5/SCL, Componente3.A5/SCL
  N4: Componente1.5V, R1.leg1, R2.Pin_0, R3.Pin_0
  GND: Componente1.GND, Componente2.GND, Componente3.GND, R1.leg2, LED1.cathode
  N5: Componente2.D9_PWM, LED1.anode
  N6: Componente3.D2, S2.Pin_3, S2.Pin_4, R2.Pin_1
  N7: Componente3.D3_PWM, S1.Pin_3, S1.Pin_4, R3.Pin_1
  N8: S1.Pin_1, S1.Pin_2
  N9: S2.Pin_1, S2.Pin_2

notes:
  Maestro
  Esclavo 10
  Esclavo 8
